# Fritzing sketch lnu_iot (saved by Fritzing 1.0.2b)
breadboards: 1

parts:
  R1 = Resistor [tolerance=±5% power=0.25W resistance=470 package=THT]
  Raspberry_Pi_Pico_W = Raspberry Pi Pico W
  LED1 = LED - 3mm [color="Red (633nm)" current=0.025A package="3 mm [THT]"]
  LED2 = LED - 3mm [color="Orange (612nm)" current=0.030A package="3 mm [THT]"]
  LED3 = LED - 3mm [color="Green (565nm)" current=0.030A package="3 mm [THT]"]
  LCD = Photocell (LDR) [power=0.25W dark_resistance_@0.01lx=300kΩ light_resistance_@100lx=400Ω luminance=10lx package=THT]
  MCP9700 = LM34 Temperature Sensor [package="TO92 [THT]"]
  DHT11 = KY-015 Temperature & Humidity Sensor Module [package="Breakout board"]

nets:
  N1: R1.Pin_0, Raspberry_Pi_Pico_W.pin_36, MCP9700.+Vs, DHT11.Vin
  N2: R1.Pin_1, Raspberry_Pi_Pico_W.pin_31, LCD.pin_0
  N3: Raspberry_Pi_Pico_W.pin_3, Raspberry_Pi_Pico_W.pin_8, Raspberry_Pi_Pico_W.pin_13, Raspberry_Pi_Pico_W.pin_18, Raspberry_Pi_Pico_W.pin_23, Raspberry_Pi_Pico_W.pin_28, Raspberry_Pi_Pico_W.pin_33, Raspberry_Pi_Pico_W.pin_38, Raspberry_Pi_Pico_W.pin_42, LED1.cathode, LED2.cathode, LED3.cathode, LCD.pin_1, MCP9700.Vout, DHT11.-
  N4: Raspberry_Pi_Pico_W.pin_25, LED1.anode
  N5: Raspberry_Pi_Pico_W.pin_26, LED2.anode
  N6: Raspberry_Pi_Pico_W.pin_27, LED3.anode
  N7: Raspberry_Pi_Pico_W.pin_29, DHT11.S
  N8: Raspberry_Pi_Pico_W.pin_30, MCP9700.GND

custom parts:
  Raspberry Pi Pico W: Raspberry Pi Pico W. Based around the RP2040 microcontroller the Pico W is a low cost microcontroller device bringing Raspberry Pi quality, cost, and easy of use to the microcontroller space. The areas marked KEEPOUT in pcb silkscreen should not have traces running through them to avoid shorts on a soldered in module!
  KY-015 Temperature & Humidity Sensor Module: KY-015 temperature and humidity sensor module, provides a low-latency serial interface to measure humidity and temperature.
